# Fritzing sketch STM32programmer2019-10-10 (saved by Fritzing 0.9.3b)
circuit board: 2.80284cm x 6.63588cm
breadboards: 1

parts:
  Part1 = BluePill
  J1 = female pin header, 4 pins [form="♀ (female)"]
  R1 = Resistor [tolerance=±5% resistance=220 package=THT]
  R2 = Resistor [tolerance=±5% resistance=4.7k package=THT]
  R3 = Resistor [tolerance=±5% resistance=4.7k package=THT]

nets:
  N1: Part1.A0, R2.Pin_1, R3.Pin_0
  N2: Part1.A5, Part1.B13, J1.pin1
  N3: Part1.3V31, J1.pin4, R2.Pin_0
  N4: Part1.GND3, J1.pin3, R3.Pin_1
  N5: Part1.B14, J1.pin2, R1.Pin_0
  N6: Part1.B12, R1.Pin_1

notes:
  June D
